// Logisim project somador_comp.circ as structural Verilog: 4 circuits, main circuit main
module main (
  input  a0,
  input  b0,
  output s0,
  output s1
);

  xor xor_1 (s0, a0, b0);
  and and_1 (s1, a0, b0);
endmodule

module meia_soma (
  input  a0,
  input  b0,
  output s0,
  output s1
);

  xor xor_1 (s0, a0, b0);
  and and_1 (s1, a0, b0);
endmodule

module soma_completa (
  input  ci0,
  input  a0,
  input  b0,
  output s0,
  output co0
);

  wire meia_soma_1_s0, meia_soma_1_s1, meia_soma_2_s1;

  meia_soma meia_soma_1 (.a0(a0), .b0(b0), .s0(meia_soma_1_s0), .s1(meia_soma_1_s1));
  meia_soma meia_soma_2 (.a0(meia_soma_1_s0), .b0(ci0), .s0(s0), .s1(meia_soma_2_s1));
  or or_1 (co0, meia_soma_2_s1, meia_soma_1_s1);
endmodule

module soma4bit (
  input  ci0,
  input  a0,
  input  b0,
  input  a1,
  input  b1,
  input  a2,
  input  b2,
  input  a3,
  input  b3,
  output s0,
  output s1,
  output s2,
  output s3,
  output co,
  output Overflow
);

  wire soma_completa_1_co0, soma_completa_2_co0, soma_completa_3_co0;

  soma_completa soma_completa_1 (.ci0(ci0), .a0(a0), .b0(b0), .s0(s0), .co0(soma_completa_1_co0));
  soma_completa soma_completa_2 (.ci0(soma_completa_1_co0), .a0(a1), .b0(b1), .s0(s1), .co0(soma_completa_2_co0));
  soma_completa soma_completa_3 (.ci0(soma_completa_2_co0), .a0(a2), .b0(b2), .s0(s2), .co0(soma_completa_3_co0));
  soma_completa soma_completa_4 (.ci0(soma_completa_3_co0), .a0(a3), .b0(b3), .s0(s3), .co0(co));
  xor xor_1 (Overflow, co, soma_completa_3_co0);
endmodule
