// Logisim project ula_4bits.circ as structural Verilog
module ula (
  input  Binvert,
  input  CarryIn,
  input  Op1,
  input  Op2,
  input  a,
  input  b,
  output Result,
  output CarryOut
);

  wire and_1_out, mux_1_s0, not_1_out, not_2_out, or_1_out, somador_completo_1_s0;

  not not_1 (not_1_out, b);
  mux mux_1 (.a(b), .b(not_1_out), .controle(Binvert), .s0(mux_1_s0));
  and and_1 (and_1_out, a, mux_1_s0);
  or or_1 (or_1_out, a, mux_1_s0);
  not not_2 (not_2_out, a);
  somador_completo somador_completo_1 (
    .ci0(CarryIn), .a0(a), .b0(mux_1_s0), .s0(somador_completo_1_s0), .co0(CarryOut));
  mux_completo mux_completo_1 (
    .a(and_1_out), .b(or_1_out), .c(not_2_out), .d(somador_completo_1_s0), .S(Result), .op1(Op1), .op2(Op2));
endmodule

module mux_completo (
  input  a,
  input  b,
  input  c,
  input  d,
  input  op1,
  input  op2,
  output S
);

  wire and_1_out, and_2_out, and_3_out, and_4_out, not_1_out, not_2_out, not_3_out, not_4_out;

  not not_1 (not_1_out, op1);
  not not_2 (not_2_out, op2);
  not not_3 (not_3_out, op1);
  not not_4 (not_4_out, op2);
  and and_1 (and_1_out, a, not_1_out, not_2_out);
  and and_2 (and_2_out, b, op2, not_3_out);
  and and_3 (and_3_out, c, not_4_out, op1);
  and and_4 (and_4_out, d, op2, op1);
  or or_1 (S, and_1_out, and_2_out, and_3_out, and_4_out);
endmodule

module mux (
  input  controle,
  input  a,
  input  b,
  output s0
);

  wire and_1_out, and_2_out, not_1_out;

  not not_1 (not_1_out, controle);
  and and_1 (and_1_out, not_1_out, a);
  and and_2 (and_2_out, controle, b);
  or or_1 (s0, and_1_out, and_2_out);
endmodule

module meia_soma (
  input  a0,
  input  b0,
  output s0,
  output s1
);

  xor xor_1 (s0, a0, b0);
  and and_1 (s1, a0, b0);
endmodule

module somador_completo (
  input  ci0,
  input  a0,
  input  b0,
  output s0,
  output co0
);

  wire meia_soma_1_s0, meia_soma_1_s1, meia_soma_2_s1;

  meia_soma meia_soma_1 (.a0(a0), .b0(b0), .s0(meia_soma_1_s0), .s1(meia_soma_1_s1));
  meia_soma meia_soma_2 (.a0(meia_soma_1_s0), .b0(ci0), .s0(s0), .s1(meia_soma_2_s1));
  or or_1 (co0, meia_soma_2_s1, meia_soma_1_s1);
endmodule

module mux_1bit (
  input  a,
  input  b,
  input  c,
  input  d,
  input  op1,
  output S
);

  wire and_1_out, and_2_out, and_3_out, and_4_out, not_1_out, not_2_out, not_3_out, not_4_out;

  and and_1 (and_1_out, a, not_1_out);
  not not_1 (not_1_out, op1);
  not not_2 (not_2_out, b);
  and and_2 (and_2_out, not_2_out, op1);
  not not_3 (not_3_out, op1);
  and and_3 (and_3_out, not_3_out, c, not_4_out);
  not not_4 (not_4_out, op1);
  and and_4 (and_4_out, d, op1);
  or or_1 (S, and_1_out, and_2_out, and_3_out, and_4_out);
endmodule

module ula_4bit (
  input  Binvert,
  input  OP1,
  input  OP2,
  input  B3,
  input  B2,
  input  B1,
  input  B0,
  input  A3,
  input  A2,
  input  A1,
  input  A0,
  output S0,
  output S1,
  output S2,
  output S3,
  output Cout
);

  wire ula_1_carryout, ula_2_carryout, ula_3_carryout;

  ula ula_1 (
    .a(A0), .b(B0), .Binvert(Binvert), .CarryIn(Binvert), .Op1(OP1), .Op2(OP2), .CarryOut(ula_1_carryout),
    .Result(S0));
  ula ula_2 (
    .a(A1), .b(B1), .Binvert(Binvert), .CarryIn(ula_1_carryout), .Op1(OP1), .Op2(OP2),
    .CarryOut(ula_2_carryout), .Result(S1));
  ula ula_3 (
    .a(A2), .b(B2), .Binvert(Binvert), .CarryIn(ula_2_carryout), .Op1(OP1), .Op2(OP2),
    .CarryOut(ula_3_carryout), .Result(S2));
  ula ula_4 (
    .a(A3), .b(B3), .Binvert(Binvert), .CarryIn(ula_3_carryout), .Op1(OP1), .Op2(OP2), .CarryOut(Cout),
    .Result(S3));
endmodule
