// Logisim project ula_simples.circ as structural Verilog
module ula (
  input  Binvert,
  input  CarryIn,
  input  Op1,
  input  Op2,
  input  a,
  input  b,
  output Result,
  output CarryOut
);

  wire and_1_out, mux_1_s0, not_1_out, not_2_out, or_1_out, somador_completo_1_s0;

  not not_1 (not_1_out, b);
  mux mux_1 (.a(b), .b(not_1_out), .controle(Binvert), .s0(mux_1_s0));
  and and_1 (and_1_out, a, mux_1_s0);
  or or_1 (or_1_out, a, mux_1_s0);
  not not_2 (not_2_out, a);
  somador_completo somador_completo_1 (
    .ci0(CarryIn), .a0(a), .b0(mux_1_s0), .s0(somador_completo_1_s0), .co0(CarryOut));
  mux_completo mux_completo_1 (
    .a(and_1_out), .b(or_1_out), .c(not_2_out), .d(somador_completo_1_s0), .S(Result), .op1(Op1), .op2(Op2));
endmodule

module mux_completo (
  input  a,
  input  b,
  input  c,
  input  d,
  input  op1,
  input  op2,
  output S
);

  wire and_1_out, and_2_out, and_3_out, and_4_out, not_1_out, not_2_out, not_3_out, not_4_out;

  not not_1 (not_1_out, op1);
  not not_2 (not_2_out, op2);
  not not_3 (not_3_out, op1);
  not not_4 (not_4_out, op2);
  and and_1 (and_1_out, a, not_1_out, not_2_out);
  and and_2 (and_2_out, b, op2, not_3_out);
  and and_3 (and_3_out, c, not_4_out, op1);
  and and_4 (and_4_out, d, op2, op1);
  or or_1 (S, and_1_out, and_2_out, and_3_out, and_4_out);
endmodule

module mux (
  input  controle,
  input  a,
  input  b,
  output s0
);

  wire and_1_out, and_2_out, not_1_out;

  not not_1 (not_1_out, controle);
  and and_1 (and_1_out, not_1_out, a);
  and and_2 (and_2_out, controle, b);
  or or_1 (s0, and_1_out, and_2_out);
endmodule

module meia_soma (
  input  a0,
  input  b0,
  output s0,
  output s1
);

  xor xor_1 (s0, a0, b0);
  and and_1 (s1, a0, b0);
endmodule

module somador_completo (
  input  ci0,
  input  a0,
  input  b0,
  output s0,
  output co0
);

  wire meia_soma_1_s0, meia_soma_1_s1, meia_soma_2_s1;

  meia_soma meia_soma_1 (.a0(a0), .b0(b0), .s0(meia_soma_1_s0), .s1(meia_soma_1_s1));
  meia_soma meia_soma_2 (.a0(meia_soma_1_s0), .b0(ci0), .s0(s0), .s1(meia_soma_2_s1));
  or or_1 (co0, meia_soma_2_s1, meia_soma_1_s1);
endmodule

module mux_1bit (
  input  a,
  input  b,
  input  c,
  input  d,
  input  op1,
  output S
);

  wire and_1_out, and_2_out, and_3_out, and_4_out, not_1_out, not_2_out, not_3_out, not_4_out;

  and and_1 (and_1_out, a, not_1_out);
  not not_1 (not_1_out, op1);
  not not_2 (not_2_out, b);
  and and_2 (and_2_out, not_2_out, op1);
  not not_3 (not_3_out, op1);
  and and_3 (and_3_out, not_3_out, c, not_4_out);
  not not_4 (not_4_out, op1);
  and and_4 (and_4_out, d, op1);
  or or_1 (S, and_1_out, and_2_out, and_3_out, and_4_out);
endmodule
