// Logisim project Questao10.circ as structural Verilog
module Somador (
  input  A,
  input  B,
  input  Cin,
  output Cout,
  output S
);

  wire and_1_out, and_2_out, xor_1_out;

  xor xor_1 (xor_1_out, A, B);
  and and_1 (and_1_out, A, B);
  or or_1 (Cout, and_1_out, and_2_out);
  xor xor_2 (S, Cin, xor_1_out);
  and and_2 (and_2_out, xor_1_out, Cin);
endmodule

module Multiplicador (
  input  A2,
  input  A1,
  input  A0,
  input  B2,
  input  B1,
  input  B0,
  output S5,
  output S4,
  output S3,
  output S2,
  output S1,
  output S0
);

  wire A0B1_out, A0B2_out, A1B0_out, A1B1_out, A1B2_out, A2B0_out, A2B1_out, and_1_out, somador_1_cout,
       somador_1_s, somador_2_cout, somador_2_s, somador_3_cout, somador_3_s, somador_4_cout, somador_4_s,
       somador_5_cout, somador_5_s, somador_6_cout, somador_6_s, somador_7_cout, somador_7_s, somador_8_cout,
       somador_8_s, somador_9_cout, somador_10_cout, somador_11_cout, somador_12_cout;

  and and_1 (and_1_out, A2, B2);
  and A0B0 (S0, A0, B0);
  and A1B2 (A1B2_out, A1, B2);
  Somador somador_1 (.A(A1B2_out), .B(A2B1_out), .Cout(somador_1_cout), .Cin(1'b0), .S(somador_1_s));
  and A2B1 (A2B1_out, A2, B1);
  and A0B2 (A0B2_out, B2, A0);
  and A1B1 (A1B1_out, A1, B1);
  and A2B0 (A2B0_out, A2, B0);
  and A0B1 (A0B1_out, A0, B1);
  and A1B0 (A1B0_out, A1, B0);
  Somador somador_2 (.A(and_1_out), .B(somador_1_cout), .Cout(somador_2_cout), .Cin(1'b0), .S(somador_2_s));
  Somador somador_3 (.A(somador_2_s), .B(somador_4_cout), .Cout(somador_3_cout), .Cin(1'b0), .S(somador_3_s));
  Somador somador_4 (.A(somador_1_s), .B(somador_6_cout), .Cout(somador_4_cout), .Cin(1'b0), .S(somador_4_s));
  Somador somador_5 (.A(A0B2_out), .B(somador_6_s), .Cout(somador_5_cout), .Cin(1'b0), .S(somador_5_s));
  Somador somador_6 (.A(A1B1_out), .B(A2B0_out), .Cout(somador_6_cout), .Cin(1'b0), .S(somador_6_s));
  Somador somador_7 (.A(somador_3_s), .B(somador_8_cout), .Cout(somador_7_cout), .Cin(1'b0), .S(somador_7_s));
  Somador somador_8 (.A(somador_4_s), .B(somador_5_cout), .Cout(somador_8_cout), .Cin(1'b0), .S(somador_8_s));
  Somador somador_9 (.A(somador_5_s), .B(somador_10_cout), .Cout(somador_9_cout), .Cin(1'b0), .S(S2));
  Somador somador_10 (.A(A0B1_out), .B(A1B0_out), .Cout(somador_10_cout), .Cin(1'b0), .S(S1));
  or or_1 (S5, somador_2_cout, somador_3_cout, somador_7_cout, somador_11_cout);
  Somador somador_11 (.A(somador_7_s), .B(somador_12_cout), .Cout(somador_11_cout), .Cin(1'b0), .S(S4));
  Somador somador_12 (.A(somador_8_s), .B(somador_9_cout), .Cout(somador_12_cout), .Cin(1'b0), .S(S3));
endmodule
